# Fritzing sketch esquema simvim G530 (saved by Fritzing 0.9.3b)

parts:
  Componente1 = Arduino Mega ADK (Rev3)
  Componente2 = Analog Digital MUX Breakout
  S1 = Momentary Switch [package=ksa_sealed_tac_switch]
  S2 = Pushbutton [package="[SMD]"]
  R1 = Resistor [tolerance=±5% resistance=220 package=THT]
  R2 = Resistor [tolerance=±5% resistance=220 package=THT]
  R3 = Resistor [tolerance=±5% resistance=220 package=THT]
  R4 = Resistor [tolerance=±5% resistance=220 package=THT]
  R5 = Resistor [tolerance=±5% resistance=220 package=THT]
  R6 = Resistor [tolerance=±5% resistance=220 package=THT]
  R7 = Resistor [tolerance=±5% resistance=220 package=THT]
  R8 = Resistor [tolerance=±5% resistance=220 package=THT]
  S3 = Pushbutton [package="[SMD]"]
  S4 = Pushbutton [package="[SMD]"]
  S5 = Pushbutton [package="[SMD]"]
  S6 = Pushbutton [package="[SMD]"]
  S7 = Pushbutton [package="[SMD]"]
  S8 = Pushbutton [package="[SMD]"]
  S9 = Pushbutton [package="[SMD]"]
  S10 = Pushbutton [package="[SMD]"]
  S11 = Pushbutton [package="[SMD]"]
  S12 = Pushbutton [package="[SMD]"]
  S13 = Pushbutton [package="[SMD]"]
  S14 = Pushbutton [package="[SMD]"]
  S15 = Pushbutton [package="[SMD]"]
  S16 = Pushbutton [package="[SMD]"]
  Componente3 = Analog Digital MUX Breakout
  RE1 = Rotary Encoder [package=THT]
  RE2 = Rotary Encoder [package=THT]
  RE3 = Rotary Encoder [package=THT]
  RE4 = Rotary Encoder [package=THT]

nets:
  VCC: Componente1.IOREF, Componente1.5V, Componente2.VCC, Componente3.VCC
  GND: Componente1.GND, Componente2.C0, Componente2.C2, Componente2.C3, Componente2.C4, Componente2.C5, Componente2.C6, Componente2.C7, Componente2.C8, Componente2.C9, Componente2.C10, Componente2.C11, Componente2.C12, Componente2.C13, Componente2.C14, Componente2.C15, Componente2.GND, Componente2.EN, S1.1, S2.Pin_1, S2.Pin_2, S3.Pin_1, S3.Pin_2, S4.Pin_1, S4.Pin_2, S5.Pin_1, S5.Pin_2, S6.Pin_1, S6.Pin_2, S7.Pin_1, S7.Pin_2, S8.Pin_1, S8.Pin_2, S9.Pin_1, S9.Pin_2, S10.Pin_1, S10.Pin_2, S11.Pin_1, S11.Pin_2, S12.Pin_1, S12.Pin_2, S13.Pin_1, S13.Pin_2, S14.Pin_1, S14.Pin_2, S15.Pin_1, S15.Pin_2, S16.Pin_1, S16.Pin_2, Componente3.GND, Componente3.EN, RE1.EncoderPinC, RE2.EncoderPinC, RE3.EncoderPinC, RE4.EncoderPinC
  N1: Componente1.D22, R4.Pin_0
  N2: Componente1.D23, R3.Pin_0
  N3: Componente1.D24, R1.Pin_0
  N4: Componente1.D25, R2.Pin_0
  N5: Componente1.D26, R5.Pin_0
  N6: Componente1.D27, R6.Pin_0
  N7: Componente1.D28, R8.Pin_0
  N8: Componente1.D29, R7.Pin_0
  N9: Componente1.D30, Componente2.SIG
  N10: Componente1.D31, Componente3.SIG
  N11: Componente2.C1, S1.2
  N12: Componente2.S0, R4.Pin_1, Componente3.S0
  N13: Componente2.S1, R3.Pin_1, Componente3.S1
  N14: Componente2.S2, R1.Pin_1, Componente3.S2
  N15: Componente2.S3, R2.Pin_1, Componente3.S3
  N16: Componente3.C0, RE1.EncoderPinA
  N17: Componente3.C1, RE1.EncoderPinB
  N18: Componente3.C2, RE2.EncoderPinA
  N19: Componente3.C3, RE2.EncoderPinB
  N20: Componente3.C4, RE3.EncoderPinA
  N21: Componente3.C5, RE3.EncoderPinB
  N22: Componente3.C6, RE4.EncoderPinA
  N23: Componente3.C7, RE4.EncoderPinB

notes:
  GPS1_CDI (1)
  GPS1_OBS (2)
  GPS1_MSG (3)
  GPS1_FPL (4)
  GPS1_VNAV (5)
  GPS1_PROC (6)
  GPS1_Zoom (14)
  GPS1_DIR (12)
  GPS1_MENU (11)
  (13)
  GPS1_CLR(10)
  GPS1_ENT (9)
  GPS1_Com_Flip (8)
  GPS1_Nav_Flip (7)
  GPS1_Nav_Com (19)
  GPS1_Cursor (24)
  GPS1_Chapter (20)
  (21)
  (23)
  (17)
  GPS1_ComNav_Coarse (15)
  (16)
  GPS1_ComNav_Fine (18)
  GPS1_Page (22)
