# Fritzing sketch mageneto 2 motores (saved by Fritzing 0.9.3b)

parts:
  Componente1 = Arduino Mega ADK (Rev3)
  Componente2 = Analog Digital MUX Breakout
  R1 = Resistor [tolerance=±5% resistance=220 package=THT]
  R2 = Resistor [tolerance=±5% resistance=220 package=THT]
  R3 = Resistor [tolerance=±5% resistance=220 package=THT]
  R4 = Resistor [tolerance=±5% resistance=220 package=THT]
  R5 = Resistor [tolerance=±5% resistance=220 package=THT]
  R6 = Resistor [tolerance=±5% resistance=220 package=THT]
  R7 = Resistor [tolerance=±5% resistance=220 package=THT]
  R8 = Resistor [tolerance=±5% resistance=220 package=THT]
  switch1 = Rotary_Switch_12x1
  switch2 = Rotary_Switch_12x1

nets:
  5V: Componente1.5V, Componente2.VCC
  N1: Componente1.D22, R4.Pin_0
  N2: Componente1.D23, R3.Pin_0
  N3: Componente1.D24, R1.Pin_0
  N4: Componente1.D25, R2.Pin_0
  N5: Componente1.D26, R5.Pin_0
  N6: Componente1.D27, R6.Pin_0
  N7: Componente1.D28, R8.Pin_0
  N8: Componente1.D29, R7.Pin_0
  N9: Componente1.D30, Componente2.SIG
  GND: Componente1.GND, Componente2.GND, Componente2.EN, switch1.0, switch2.0
  N10: Componente2.C0, switch1.1
  N11: Componente2.C1, switch1.2
  N12: Componente2.C2, switch1.3
  N13: Componente2.C3, switch1.4
  N14: Componente2.C4, switch1.5
  N15: Componente2.C5, switch2.1
  N16: Componente2.C6, switch2.2
  N17: Componente2.C7, switch2.3
  N18: Componente2.C8, switch2.4
  N19: Componente2.C9, switch2.5
  N20: Componente2.S0, R4.Pin_1
  N21: Componente2.S1, R3.Pin_1
  N22: Componente2.S2, R1.Pin_1
  N23: Componente2.S3, R2.Pin_1

notes:
  Starter_Key_Eng1 (1)
  (2)
  (3)
  (4)
  (7)
  (8)
  (9)
  (10)
  (5)
  Starter_Key_Eng2 (6)
