# Fritzing sketch panel de audio (saved by Fritzing 0.9.3b)

parts:
  Componente1 = Arduino Mega ADK (Rev3)
  Componente2 = Analog Digital MUX Breakout
  R1 = Resistor [tolerance=±5% resistance=220 package=THT]
  R2 = Resistor [tolerance=±5% resistance=220 package=THT]
  R3 = Resistor [tolerance=±5% resistance=220 package=THT]
  R4 = Resistor [tolerance=±5% resistance=220 package=THT]
  R5 = Resistor [tolerance=±5% resistance=220 package=THT]
  R6 = Resistor [tolerance=±5% resistance=220 package=THT]
  R7 = Resistor [tolerance=±5% resistance=220 package=THT]
  R8 = Resistor [tolerance=±5% resistance=220 package=THT]
  Componente3 = Analog Digital MUX Breakout
  J1 = Camdenboss CTB0158-2 [part_number=CTB0158-2 package=THT]
  LED1 = smd LED [color="Green (555nm)" package="0805 [SMD]"]
  U3 = STP16CP05 [package=so-24dw]
  R10 = Resistor [tolerance=±5% resistance=1k package="0402 [SMD]"]
  LED2 = smd LED [color="Green (555nm)" package="0805 [SMD]"]
  LED3 = smd LED [color="Green (555nm)" package="0805 [SMD]"]
  LED4 = smd LED [color="Green (555nm)" package="0805 [SMD]"]
  LED5 = smd LED [color="Green (555nm)" package="0805 [SMD]"]
  LED6 = smd LED [color="Green (555nm)" package="0805 [SMD]"]
  LED7 = smd LED [color="Green (555nm)" package="0805 [SMD]"]
  LED8 = smd LED [color="Green (555nm)" package="0805 [SMD]"]
  LED9 = smd LED [color="White (4500K)" package="0805 [SMD]"]
  LED10 = smd LED [color="Blue (430nm)" package="0805 [SMD]"]
  LED11 = smd LED [color="Red (633nm)" package="0805 [SMD]"]
  S1 = Momentary Switch [package=ksa_sealed_tac_switch]
  S2 = Momentary Switch [package=ksa_sealed_tac_switch]
  S3 = Momentary Switch [package=ksa_sealed_tac_switch]
  S4 = Momentary Switch [package=ksa_sealed_tac_switch]
  S5 = Momentary Switch [package=ksa_sealed_tac_switch]
  S6 = Momentary Switch [package=ksa_sealed_tac_switch]
  S7 = Momentary Switch [package=ksa_sealed_tac_switch]
  S8 = Momentary Switch [package=ksa_sealed_tac_switch]

nets:
  GND: Componente1.GND, Componente2.GND, Componente2.EN, Componente3.GND, J1.pin1, U3.GND, U3.~OE, R10.Pin_1, S1.3, S2.3, S3.3, S4.3, S5.3, S6.3, S7.3, S8.3
  N1: Componente1.D22, R4.Pin_0
  N2: Componente1.D23, R3.Pin_0
  N3: Componente1.D24, R1.Pin_0
  N4: Componente1.D25, R2.Pin_0
  N5: Componente1.D26, R5.Pin_0
  N6: Componente1.D27, R6.Pin_0
  N7: Componente1.D28, R8.Pin_0
  N8: Componente1.D29, R7.Pin_0
  N9: Componente1.D30, Componente2.SIG
  N10: Componente1.D31, Componente3.EN
  N11: Componente2.C0, S8.4
  N12: Componente2.C1, S7.4
  N13: Componente2.C2, S6.4
  N14: Componente2.C3, S5.4
  N15: Componente2.C4, S4.4
  N16: Componente2.C5, S3.4
  N17: Componente2.C6, S2.4
  N18: Componente2.C7, S1.4
  VCC: Componente2.VCC, Componente3.VCC, J1.pin2, LED1.anode, U3.VDD, LED2.anode, LED3.anode, LED4.anode, LED5.anode, LED6.anode, LED7.anode, LED8.anode, LED9.anode, LED10.anode, LED11.anode
  N19: Componente2.S0, R4.Pin_1, Componente3.S0
  N20: Componente2.S1, R3.Pin_1, Componente3.S1
  N21: Componente2.S2, R1.Pin_1, Componente3.S2
  N22: Componente2.S3, R2.Pin_1, Componente3.S3
  N23: R5.Pin_1, Componente3.SIG
  N24: R6.Pin_1, U3.LE
  N25: R8.Pin_1, U3.SDI
  N26: Componente3.C9, U3.CLK
  N27: LED1.cathode, U3.OUT0
  N28: U3.OUT1, LED2.cathode
  N29: U3.OUT2, LED3.cathode
  N30: U3.OUT3, LED4.cathode
  N31: U3.OUT4, LED5.cathode
  N32: U3.OUT5, LED6.cathode
  N33: U3.OUT6, LED7.cathode
  N34: U3.OUT7, LED8.cathode
  N35: U3.OUT8, LED9.cathode
  N36: U3.OUT9, LED11.cathode
  N37: U3.OUT10, LED10.cathode
  N38: U3.REXT, R10.Pin_0

notes:
  S0
  S1
  S2
  S3
  SIG
  L
  D
  T
  GND
  +5V
  DM13A
  Com1_Audio_Switch
  Com2_Audio_Switch
  Nav1_Audio_Switch
  Nav2_Audio_Switch
  ADF1_Audio_Switch
  ADF2_Audio_Switch
  DME_Audio_Switch
  Beacon_Audio_Switch
  Com1_Audio_LED
  Com2_Audio_LED
  Nav1_Audio_LED
  Nav2_Audio_LED
  ADF1_Audio_LED
  ADF2_Audio_LED
  DME_Audio_LED
  Beacon_Audio_LED
  Over_O_Marker
  Over_M_Marker
  Over_I_Marker
