# Fritzing sketch panel de luces (saved by Fritzing 0.9.3b)

parts:
  Componente1 = Arduino Mega ADK (Rev3)
  Componente2 = Analog Digital MUX Breakout
  R1 = Resistor [tolerance=±5% resistance=220 package=THT]
  R2 = Resistor [tolerance=±5% resistance=220 package=THT]
  R3 = Resistor [tolerance=±5% resistance=220 package=THT]
  R4 = Resistor [tolerance=±5% resistance=220 package=THT]
  R5 = Resistor [tolerance=±5% resistance=220 package=THT]
  R6 = Resistor [tolerance=±5% resistance=220 package=THT]
  R7 = Resistor [tolerance=±5% resistance=220 package=THT]
  R8 = Resistor [tolerance=±5% resistance=220 package=THT]
  J1 = Camdenboss CTB0158-2 [part_number=CTB0158-2 package=THT]
  S9 = Taiway 100-SP-X-T1 SPDT Miniature Toggle Switch [part_number=100-SP-X-T1-0-0-B1-M1 package=THT]
  S10 = Taiway 100-SP-X-T1 SPDT Miniature Toggle Switch [part_number=100-SP-X-T1-0-0-B1-M1 package=THT]
  S11 = Taiway 100-SP-X-T1 SPDT Miniature Toggle Switch [part_number=100-SP-X-T1-0-0-B1-M1 package=THT]
  S12 = Taiway 100-SP-X-T1 SPDT Miniature Toggle Switch [part_number=100-SP-X-T1-0-0-B1-M1 package=THT]
  S13 = Taiway 100-SP-X-T1 SPDT Miniature Toggle Switch [part_number=100-SP-X-T1-0-0-B1-M1 package=THT]
  S14 = Taiway 100-SP-X-T1 SPDT Miniature Toggle Switch [part_number=100-SP-X-T1-0-0-B1-M1 package=THT]
  S15 = Taiway 100-SP-X-T1 SPDT Miniature Toggle Switch [part_number=100-SP-X-T1-0-0-B1-M1 package=THT]
  S16 = Taiway 100-SP-X-T1 SPDT Miniature Toggle Switch [part_number=100-SP-X-T1-0-0-B1-M1 package=THT]
  S17 = Taiway 100-SP-X-T1 SPDT Miniature Toggle Switch [part_number=100-SP-X-T1-0-0-B1-M1 package=THT]

nets:
  GND: Componente1.GND, Componente2.GND, Componente2.EN, J1.pin1, S9.COM
  N1: Componente1.D22, R4.Pin_0
  N2: Componente1.D23, R3.Pin_0
  N3: Componente1.D24, R1.Pin_0
  N4: Componente1.D25, R2.Pin_0
  N5: Componente1.D26, R5.Pin_0
  N6: Componente1.D27, R6.Pin_0
  N7: Componente1.D28, R8.Pin_0
  N8: Componente1.D29, R7.Pin_0
  N9: Componente1.D30, Componente2.SIG
  N10: Componente2.C0, S13.L2
  N11: Componente2.C1, S12.L2
  N12: Componente2.C2, S11.L2
  N13: Componente2.C3, S10.L2
  N14: Componente2.C4, S9.L2
  N15: Componente2.C5, S14.L2
  N16: Componente2.C6, S15.L2
  N17: Componente2.C7, S16.L2
  N18: Componente2.C8, S17.L2
  N19: Componente2.VCC, J1.pin2
  N20: Componente2.S0, R4.Pin_1
  N21: Componente2.S1, R3.Pin_1
  N22: Componente2.S2, R1.Pin_1
  N23: Componente2.S3, R2.Pin_1
  N24: J1.terminal_1, S12.COM, S13.COM, S14.COM, S15.COM, S16.COM, S17.COM

notes:
  S0
  S1
  S2
  S3
  SIG
  L
  D
  T
  GND
  +5V
  Beacon_Light
  Landing_Lights
  Taxi_Lights
  Nav_Lights
  Strobe_Light
  Wing_Lights
  Recog_Light
  Panel_Lights
  Panel_Light_Switch

custom parts:
  Taiway 100-SP-X-T1 SPDT Miniature Toggle Switch: Taiway SP1-T1 SPDT Miniature Toggle Switch. This switch has two or three positions, the function of which varies depending on the exact model: Position Model \_ _|_ _/ SP-1 On None On SP-2 On None (On) SP-3 On Off On SP-4 (On) Off (On) SP-5 On Off (On) This part will suffice for all 5 model variations, but is important the designer specifies clearly which model is intended. The breadboard view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
