# Fritzing sketch panel de radio (saved by Fritzing 0.9.3b)

parts:
  Componente1 = Arduino Mega ADK (Rev3)
  Componente2 = Analog Digital MUX Breakout
  R1 = Resistor [tolerance=±5% resistance=220 package=THT]
  R2 = Resistor [tolerance=±5% resistance=220 package=THT]
  R3 = Resistor [tolerance=±5% resistance=220 package=THT]
  R4 = Resistor [tolerance=±5% resistance=220 package=THT]
  R5 = Resistor [tolerance=±5% resistance=220 package=THT]
  R6 = Resistor [tolerance=±5% resistance=220 package=THT]
  R7 = Resistor [tolerance=±5% resistance=220 package=THT]
  R8 = Resistor [tolerance=±5% resistance=220 package=THT]
  DISPLAY_8_DIGITOS1 = 7-Segment LED Display 8 Digitos [package=THT]
  DISPLAY_8_DIGITOS2 = 7-Segment LED Display 8 Digitos [package=THT]
  Componente3 = Analog Digital MUX Breakout
  U1 = ENCODER-QUADRATURE [package=encoder-16mm-quad]
  U2 = ENCODER-QUADRATURE [package=encoder-16mm-quad]
  S1 = Pushbutton [package="[THT]"]
  J1 = Camdenboss CTB0158-2 [part_number=CTB0158-2 package=THT]
  R9 = Resistor [tolerance=±5% resistance=1k package="0402 [SMD]"]
  R10 = Resistor [tolerance=±5% resistance=1k package="0402 [SMD]"]
  Componente4 = Analog Digital MUX Breakout

nets:
  GND: Componente1.GND, Componente2.GND, Componente2.EN, DISPLAY_8_DIGITOS1.pin_2, DISPLAY_8_DIGITOS2.pin_2, Componente3.GND, U1.B, U2.B, S1.Pin_1, S1.Pin_2, J1.pin1, R9.Pin_0, R10.Pin_0
  N1: Componente1.D22, R4.Pin_0
  N2: Componente1.D23, R3.Pin_0
  N3: Componente1.D24, R1.Pin_0
  N4: Componente1.D25, R2.Pin_0
  N5: Componente1.D26, R5.Pin_0
  N6: Componente1.D27, R6.Pin_0
  N7: Componente1.D28, R8.Pin_0
  N8: Componente1.D29, R7.Pin_0
  N9: Componente1.D30, Componente2.SIG
  N10: Componente1.D31, Componente3.EN
  N11: Componente1.D32, Componente4.SIG
  N12: Componente2.C0, S1.Pin_3, S1.Pin_4
  N13: Componente2.C1, U1.C
  N14: Componente2.C2, U1.A
  N15: Componente2.C3, U2.C
  N16: Componente2.C4, U2.A
  VCC: Componente2.VCC, DISPLAY_8_DIGITOS1.pin_1, DISPLAY_8_DIGITOS2.pin_1, Componente3.VCC, J1.pin2
  N17: Componente2.S0, R4.Pin_1, Componente3.S0
  N18: Componente2.S1, R3.Pin_1, Componente3.S1
  N19: Componente2.S2, R1.Pin_1, Componente3.S2
  N20: Componente2.S3, R2.Pin_1, Componente3.S3
  N21: R5.Pin_1, Componente3.SIG
  N22: R6.Pin_1, DISPLAY_8_DIGITOS1.pin_4, DISPLAY_8_DIGITOS2.pin_4
  N23: R8.Pin_1, DISPLAY_8_DIGITOS1.pin_3, DISPLAY_8_DIGITOS2.pin_3
  N24: DISPLAY_8_DIGITOS1.pin_5, Componente3.C0, R9.Pin_1
  N25: DISPLAY_8_DIGITOS2.pin_5, Componente3.C1, R10.Pin_1

notes:
  S0
  S1
  S2
  S3
  SIG
  L
  D
  T
  Com1_Stby_FLIP (1)
  Com1_Stby_Mhz_Set (2)
  Com1_Stby_k5_Set (4)
  (3)
  (5)
  GND
  +5V
  Com2_Stby_FLIP (6)
  Com2_Stby_Mhz_Set (7)
  (8)
  Com2_Stby_k5_Set (9)
  (13)
  Nav1_Stby_Mhz_Set (12)
  Nav1_FLIP (11)
  (10)
  Nav1_Stby_khz_Set (14)
  (15)
  Nav2_FLIP (15)
  Nav2_Stby_Mhz_Set (16)
  Nav2_Stby_khz_Set (18)
  (17)
  Com1_Active_6 (19)
  Com1_Stby_6 (20)
  Com2_Active_6 (21)
  Com2_Stby_6 (22)
  Nav1_Active (23)
  Nav1_Stby (24)
  Nav2_Active (25)
  Nav2_Stby (26)
