# Fritzing sketch panel de transponder (saved by Fritzing 0.9.3b)

parts:
  Componente1 = Arduino Mega ADK (Rev3)
  Componente2 = Analog Digital MUX Breakout
  R1 = Resistor [tolerance=±5% resistance=220 package=THT]
  R2 = Resistor [tolerance=±5% resistance=220 package=THT]
  R3 = Resistor [tolerance=±5% resistance=220 package=THT]
  R4 = Resistor [tolerance=±5% resistance=220 package=THT]
  R5 = Resistor [tolerance=±5% resistance=220 package=THT]
  R6 = Resistor [tolerance=±5% resistance=220 package=THT]
  R7 = Resistor [tolerance=±5% resistance=220 package=THT]
  R8 = Resistor [tolerance=±5% resistance=220 package=THT]
  DISPLAY_8_DIGITOS1 = 7-Segment LED Display 8 Digitos [package=THT]
  Componente3 = Analog Digital MUX Breakout
  U1 = ENCODER-QUADRATURE [package=encoder-16mm-quad]
  U2 = ENCODER-QUADRATURE [package=encoder-16mm-quad]
  J1 = Camdenboss CTB0158-2 [part_number=CTB0158-2 package=THT]
  R9 = Resistor [tolerance=±5% resistance=1k package="0402 [SMD]"]
  switch1 = Rotary_Switch_12x1
  LED1 = smd LED [color="Green (555nm)" package="0805 [SMD]"]
  U3 = STP16CP05 [package=so-24dw]
  R10 = Resistor [tolerance=±5% resistance=1k package="0402 [SMD]"]

nets:
  GND: Componente1.GND, Componente2.GND, Componente2.EN, DISPLAY_8_DIGITOS1.pin_2, Componente3.GND, U1.B, U2.B, J1.pin1, R9.Pin_0, switch1.0, U3.GND, U3.~OE, R10.Pin_1
  N1: Componente1.D22, R4.Pin_0
  N2: Componente1.D23, R3.Pin_0
  N3: Componente1.D24, R1.Pin_0
  N4: Componente1.D25, R2.Pin_0
  N5: Componente1.D26, R5.Pin_0
  N6: Componente1.D27, R6.Pin_0
  N7: Componente1.D28, R8.Pin_0
  N8: Componente1.D29, R7.Pin_0
  N9: Componente1.D30, Componente2.SIG
  N10: Componente1.D31, Componente3.EN
  N11: Componente2.C0, U1.C
  N12: Componente2.C1, U1.A
  N13: Componente2.C2, U2.C
  N14: Componente2.C3, U2.A
  N15: Componente2.C4, switch1.12
  N16: Componente2.C5, switch1.1
  N17: Componente2.C6, switch1.2
  N18: Componente2.C7, switch1.3
  N19: Componente2.C8, switch1.4
  N20: Componente2.C9, switch1.5
  VCC: Componente2.VCC, DISPLAY_8_DIGITOS1.pin_1, Componente3.VCC, J1.pin2, LED1.anode, U3.VDD
  N21: Componente2.S0, R4.Pin_1, Componente3.S0
  N22: Componente2.S1, R3.Pin_1, Componente3.S1
  N23: Componente2.S2, R1.Pin_1, Componente3.S2
  N24: Componente2.S3, R2.Pin_1, Componente3.S3
  N25: R5.Pin_1, Componente3.SIG
  N26: R6.Pin_1, DISPLAY_8_DIGITOS1.pin_4, U3.LE
  N27: R8.Pin_1, DISPLAY_8_DIGITOS1.pin_3, U3.SDI
  N28: DISPLAY_8_DIGITOS1.pin_5, Componente3.C0, R9.Pin_1
  N29: Componente3.C9, U3.CLK
  N30: LED1.cathode, U3.OUT0
  N31: U3.REXT, R10.Pin_0

notes:
  S0
  S1
  S2
  S3
  SIG
  L
  D
  T
  XPDR_1_2_Set (1)
  XPDR_3_4_Set (3)
  (2)
  (4)
  GND
  +5V
  DM13A
  XPDR_Mode_OFF (5)
  XPDR_Mode_STBY (6)
  XPDR_Mode_ON (7)
  XPDR_Mode_TEST (8)
  XPDR_Mode_GND (9)
  XPDR_Mode_ALT (10)
  XPDR_LIT_LED (11)
  XPDR_CODE (12)
