# Fritzing sketch esquema simvim tren aterrizaje (saved by Fritzing 0.9.3b)

parts:
  Componente1 = Arduino Mega ADK (Rev3)
  Componente2 = Analog Digital MUX Breakout
  S1 = Momentary Switch [package=ksa_sealed_tac_switch]
  S2 = Pushbutton [package="[SMD]"]
  Componente3 = Analog Digital MUX Breakout
  R1 = Resistor [tolerance=±5% resistance=220 package=THT]
  R2 = Resistor [tolerance=±5% resistance=220 package=THT]
  R3 = Resistor [tolerance=±5% resistance=220 package=THT]
  R4 = Resistor [tolerance=±5% resistance=220 package=THT]
  R5 = Resistor [tolerance=±5% resistance=220 package=THT]
  R6 = Resistor [tolerance=±5% resistance=220 package=THT]
  R7 = Resistor [tolerance=±5% resistance=220 package=THT]
  R8 = Resistor [tolerance=±5% resistance=220 package=THT]
  U1 = STP16CP05 [package=so-24dw]
  R9 = Resistor [tolerance=±5% resistance=1k package=THT]
  LED1 = LED - 5mm [color="Red (633nm)" package="5 mm [THT]"]
  LED2 = smd LED [color="Red (633nm)" package="1206 [SMD]"]
  LED3 = smd LED [color="Red (633nm)" package="1206 [SMD]"]
  LED4 = smd LED [color="Green (570nm)" package="1206 [SMD]"]
  LED5 = smd LED [color="Green (570nm)" package="1206 [SMD]"]
  LED6 = smd LED [color="Green (570nm)" package="1206 [SMD]"]

nets:
  VCC: Componente1.5V, Componente2.VCC, Componente3.VCC, U1.VDD
  N1: Componente1.D22, R4.Pin_0
  N2: Componente1.D23, R3.Pin_0
  N3: Componente1.D24, R1.Pin_0
  N4: Componente1.D25, R2.Pin_0
  N5: Componente1.D26, R5.Pin_0
  N6: Componente1.D27, R6.Pin_0
  N7: Componente1.D28, R8.Pin_0
  N8: Componente1.D29, R7.Pin_0
  N9: Componente1.D30, Componente2.SIG
  N10: Componente1.D31, Componente3.EN
  GND: Componente1.GND, Componente2.GND, Componente2.EN, S1.1, S2.Pin_1, S2.Pin_2, Componente3.GND, U1.GND, U1.OUT15, U1.~OE, R9.Pin_1
  N11: Componente2.C0, S1.3
  N12: Componente2.C1, S2.Pin_3, S2.Pin_4
  N13: Componente2.S0, Componente3.S0, R4.Pin_1
  N14: Componente2.S1, Componente3.S1, R3.Pin_1
  N15: Componente2.S2, Componente3.S2, R1.Pin_1
  N16: Componente2.S3, Componente3.S3, R2.Pin_1
  N17: Componente3.C0, U1.CLK
  N18: Componente3.SIG, R5.Pin_1
  N19: R6.Pin_1, U1.LE
  N20: R8.Pin_1, U1.SDI
  N21: U1.OUT0, LED4.cathode
  N22: U1.OUT1, LED5.cathode
  N23: U1.OUT2, LED6.cathode
  N24: U1.OUT3, LED1.cathode
  N25: U1.OUT4, LED2.cathode
  N26: U1.OUT5, U1.OUT6, LED3.cathode
  N27: U1.SDO, U1.REXT, R9.Pin_0
  N28: LED1.anode, LED2.anode, LED3.anode, LED4.anode, LED5.anode, LED6.anode

notes:
  Gear_Lever_UP
  Gear_Lever_DN
  V_led
  Right_Gear_Green
  Left_Gear_Green
  Nose_Gear_Green
  Righ_Gear_Red
  Left_Gear_Red
  Nose_Gear_Red
  DM13A
